// Logisim project 1.circ as structural Verilog: 1 circuit, main circuit main
module main (
  input  in_1,
  input  in_2,
  input  in_3,
  input  in_4,
  output out_5,
  output out_6,
  output out_7,
  output out_8
);

  wire clock_1_out;

  Clock clock_1 (.out(clock_1_out));
  D_Flip_Flop d_ff_1 (.D(in_1), .Q(out_5));  // open: clk, Qn, preset, en, reset
  D_Flip_Flop d_ff_2 (.clk(clock_1_out), .Q(out_6));  // open: D, Qn, preset, en, reset
  D_Flip_Flop d_ff_3 (.clk(clock_1_out), .Q(out_7));  // open: D, Qn, preset, en, reset
  D_Flip_Flop d_ff_4 (.clk(clock_1_out), .Q(out_8));  // open: D, Qn, preset, en, reset
endmodule
