// Logisim project 2.circ as structural Verilog: 1 circuit, main circuit main
module main (
  input  in_1,
  output out_2,
  output out_3
);

  wire and_1_out, and_2_out, and_3_out, and_4_out, clock_1_out, nand_1_out, not_1_out, not_2_out, not_3_out;

  not not_1 (not_1_out, in_1);
  and and_1 (and_1_out, not_2_out, not_2_out, not_1_out);
  and and_2 (and_2_out, not_2_out, in_1, in_1);
  not not_2 (not_2_out, clock_1_out);
  not nand_1 (nand_1_out, and_1_out);  // NAND_Gate
  // NAND_Gate nand_2 has open pins: in1=nand_1_out, in2=and_2_out, out=open
  Clock clock_1 (.out(clock_1_out));
  not not_3 (not_3_out, nand_1_out);
  and and_3 (and_3_out, clock_1_out, clock_1_out, not_3_out);
  and and_4 (and_4_out, clock_1_out, nand_1_out, nand_1_out);
  nand nand_3 (out_2, and_3_out, out_3);
  nand nand_4 (out_3, out_2, and_4_out);
endmodule
