// Logisim project 3.circ as structural Verilog: 1 circuit, main circuit main
module main (
  input  in_1,
  input  in_2,
  input  in_3,
  output out_4,
  output out_5,
  output out_6,
  output out_7
);

  wire and_1_out, and_2_out, clock_1_out, not_1_out;

  Clock clock_1 (.out(clock_1_out));
  nand nand_1 (out_4, in_1, out_5);
  nand nand_2 (out_5, out_4, in_2);
  not not_1 (not_1_out, in_3);
  and and_1 (and_1_out, clock_1_out, clock_1_out, not_1_out);
  and and_2 (and_2_out, clock_1_out, in_3, in_3);
  nand nand_3 (out_6, and_1_out, out_7);
  nand nand_4 (out_7, out_6, and_2_out);
endmodule
